# Fritzing sketch Car wiring diagram (saved by Fritzing 0.9.3b)
breadboards: 1

parts:
  Part1 = Bluetooth HC-05 Macho
  hc-sr1 = hc-sr04
  L298N1 = L298N DC motor driver
  M1 = Getriebemotor
  M2 = Getriebemotor
  Pico_H1 = Raspberry Pi Pico H
  VCC1 = Battery block 9V

nets:
  N1: Part1.TXD, Pico_H1.GP1
  N2: Part1.RXD, Pico_H1.GP0
  VCC: Part1.VCC, hc-sr1.VCC, L298N1.5V, Pico_H1.VSYS
  GND: Part1.GND, hc-sr1.GND, L298N1.GND, Pico_H1.GND, VCC1.-
  N3: hc-sr1.Trig, Pico_H1.GP21
  N4: hc-sr1.Echo, Pico_H1.GP20
  N5: L298N1.OUT1, M1.pin_2
  N6: L298N1.OUT2, M1.pin_1
  N7: L298N1.OUT3, M2.pin_2
  N8: L298N1.OUT4, M2.pin_1
  N9: L298N1.ENA, Pico_H1.GP8
  N10: L298N1.ENB, Pico_H1.GP2
  N11: L298N1.IN1, Pico_H1.GP7
  N12: L298N1.IN2, Pico_H1.GP6
  N13: L298N1.IN3, Pico_H1.GP4
  N14: L298N1.IN4, Pico_H1.GP3

custom parts:
  L298N DC motor driver: 2x DC motor driver with 78M05 positive voltage regulator (7..35 V) L298N: max 46 V, 2 A Set 5 V Enable jumper to enable 5 V regultor (needed for the L298N) and +5 V output at screw terminal or supply external +5 V at screw terminal Set ENA and/or ENB to +5 V to enable motor permanently or supply ENA and/or ENB with PWM signal IN1 and IN2 set rotation directory for motor A (OUT1/OUT2) IN2 and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
  Raspberry Pi Pico H: Raspberry Pi Pico H. Based around the RP2040 microcontroller the Pico H is a low cost microcontroller device bringing Raspberry Pi quality, cost, and easy of use to the microcontroller space.
  Battery block 9V: 9 Volt battery block with 200mil pcb footprint spacing
